# Fritzing sketch mkr-vl53l0x-sensor-circuit-diagram (saved by Fritzing 0.9.4)
breadboards: 1

parts:
  Part1 = Arduino MKR WiFi 1010
  Part5 = GY-VL53L0XV2 Laser Ranger Module

nets:
  N1: Part1.D11_SDA, Part5.SDA
  N2: Part1.D12_SCL, Part5.SCL
  GND: Part1.GND, Part5.GND
  VCC: Part1.VCC, Part5.VCC

custom parts:
  Arduino MKR WiFi 1010: This is the newest version of the MKR 1000 WIFI, but with an ESP32 module on board made by U-BLOX.
  GY-VL53L0XV2 Laser Ranger Module: The GY-VL53L0XV2 is based on the VL53L0X from ST Microelectronics, a time-of-flight ranging system integrated into a compact module.
