# Fritzing sketch uno-vl53l0x-sensor-circuit-diagram (saved by Fritzing 0.9.4)
breadboards: 1

parts:
  Part2 = Arduino Uno (Rev3)
  Part4 = GY-VL53L0XV2 Laser Ranger Module

nets:
  N1: Part2.A4/SDA, Part4.SDA
  N2: Part2.A5/SCL, Part4.SCL
  3V3: Part2.3V3, Part4.VCC
  GND: Part2.GND, Part4.GND

custom parts:
  GY-VL53L0XV2 Laser Ranger Module: The GY-VL53L0XV2 is based on the VL53L0X from ST Microelectronics, a time-of-flight ranging system integrated into a compact module.
