# Fritzing sketch esp32-vl53l0x-sensor-circuit-diagram (saved by Fritzing 0.9.4)
breadboards: 1

parts:
  MCU1 = Wemos Lolin32lite
  Part3 = GY-VL53L0XV2 Laser Ranger Module

nets:
  N1: MCU1.pin_13, Part3.GND
  N2: MCU1.pin_20, Part3.SDA
  N3: MCU1.pin_23, Part3.SCL
  N4: MCU1.pin_28, Part3.VCC

custom parts:
  Wemos Lolin32lite: Wemos Lolinlite32 wifi and bluetooth board based on the ESP-32 cpu, digital I/Os 19, analog inputs 6, clock 240mhz, Flash 4Mbytes, lipo battery charger (500ma connection broken out on breadboard but not pcb), usb.
  GY-VL53L0XV2 Laser Ranger Module: The GY-VL53L0XV2 is based on the VL53L0X from ST Microelectronics, a time-of-flight ranging system integrated into a compact module.
