# Fritzing sketch esp8266-vl53l0x-sensor-circuit-diagram (saved by Fritzing 0.9.3b)
breadboards: 1

parts:
  Part2 = GY-VL53L0XV2 Laser Ranger Module
  WeMos_D1_Mini1 = WeMos D1 Mini

nets:
  VCC: Part2.VCC, WeMos_D1_Mini1.3V3
  N1: Part2.GND, WeMos_D1_Mini1.G
  N2: Part2.SCL, WeMos_D1_Mini1.D1
  N3: Part2.SDA, WeMos_D1_Mini1.D2

custom parts:
  GY-VL53L0XV2 Laser Ranger Module: The GY-VL53L0XV2 is based on the VL53L0X from ST Microelectronics, a time-of-flight ranging system integrated into a compact module.
