# Fritzing sketch rpi-vl53l0x-sensor-circuit-diagram (saved by Fritzing 0.9.3b)
breadboards: 1

parts:
  Raspberry_Pi_1 = Raspberry Pi 3 [part_number=RPI-3-V1.2]
  Part2 = GY-VL53L0XV2 Laser Ranger Module

nets:
  3V3: Raspberry_Pi_1.3v3, Part2.VCC
  N1: Raspberry_Pi_1.GPIO2, Part2.SDA
  N2: Raspberry_Pi_1.GPIO3, Part2.SCL
  GND: Raspberry_Pi_1.GND, Part2.GND

custom parts:
  GY-VL53L0XV2 Laser Ranger Module: The GY-VL53L0XV2 is based on the VL53L0X from ST Microelectronics, a time-of-flight ranging system integrated into a compact module.
